# Fritzing sketch DC_motor_Max_ToArduino_skematics (saved by Fritzing 0.9.3b)
breadboards: 1

parts:
  Q1 = Basic FET N-Channel [part_number=tip122 package="DPak [SMD]"]
  R1 = Resistor [tolerance=±5% resistance=2.2k package="0603 [SMD]"]
  Part1 = Arduino Uno (Rev3)
  VCC1 = Battery block 9V
  M1 = DC Motor
  D1 = Diode [package=diode-1n4001]  # not connected
  Q2 = MOSFET-NCHANNEL [part_number=IRF510 package=to220v]
  R2 = Resistor [tolerance=±5% resistance=10k package="0603 [SMD]"]
  D2 = Diode [package=diode-1n4001]
  M2 = DC Motor
  R3 = Resistor [tolerance=±5% resistance=10k package="0603 [SMD]"]

nets:
  N1: Q1.Gate, R1.Pin_1, R3.Pin_0
  N2: Q1.drain, M1.pin_2
  N3: Q1.source, Part1.GND, VCC1.-, Q2.S, R2.Pin_1, R3.Pin_1
  N4: R1.Pin_0, Part1.D9_PWM
  N5: Part1.D3_PWM, Q2.G, R2.Pin_0
  N6: VCC1.+, M1.pin_1, M2.pin_1
  N7: Q2.D, D2.A, M2.pin_2
